# Fritzing sketch FritzingSetup (saved by Fritzing 0.9.3b)
breadboards: 1

parts:
  Part1 = Adafruit T-Cobbler Plus [part_number="Adafruit #1989 and #2028"]
  Raspberry_Pi_1 = Raspberry Pi 3 [part_number=RPI-3-V1.2]
  S1 = Momentary Switch [package=ksa_sealed_tac_switch]
  S2 = Momentary Switch [package=ksa_sealed_tac_switch]
  R1 = Resistor [tolerance=±5% resistance=220 package="1206 [SMD]"]
  R2 = Resistor [tolerance=±5% resistance=220 package="1206 [SMD]"]  # not connected
  Part2 = Arduino Uno (Rev3) - ICSP
  LED1 = RGB LED (com. anode, rbg) [package="5 mm [THT]"]
  R3 = Resistor [tolerance=±5% resistance=220 package="1206 [SMD]"]
  R4 = Resistor [tolerance=±5% resistance=220 package="1206 [SMD]"]
  R5 = Resistor [tolerance=±5% resistance=220 package="1206 [SMD]"]
  LED2 = RGB LED (com. anode, rbg) [package="5 mm [THT]"]

nets:
  3V3: Part1.+3.3V, Part1.+3.3V_2, Raspberry_Pi_1.3v3, Raspberry_Pi_1.3V3, R1.Pin_0
  N1: Part1.SDA, Raspberry_Pi_1.GPIO2
  N2: Part1.SCL, Raspberry_Pi_1.GPIO3
  N3: Part1.GPIO4, Raspberry_Pi_1.GPIO4, S2.4
  GND: Part1.GND, Raspberry_Pi_1.GND, S1.2, S2.2, LED2.common_anode
  N4: Part1.GPIO17, Raspberry_Pi_1.GPIO17, S1.4, R1.Pin_1
  N5: Part1.GPIO27, Raspberry_Pi_1.GPIO27
  N6: Part1.GPIO22, Raspberry_Pi_1.GPIO22
  N7: Part1.MOSI, Raspberry_Pi_1.GPIO10
  N8: Part1.MISO, Raspberry_Pi_1.GPIO9
  N9: Part1.SCLK, Raspberry_Pi_1.GPIO11
  N10: Part1.EEDAT, Raspberry_Pi_1.ID_SD
  N11: Part1.GPIO5, Raspberry_Pi_1.GPIO5
  N12: Part1.GPIO6, Raspberry_Pi_1.GPIO6
  N13: Part1.GPIO13, Raspberry_Pi_1.GPIO13
  N14: Part1.GPIO19, Raspberry_Pi_1.GPIO19
  N15: Part1.GPIO26, Raspberry_Pi_1.GPIO26
  +5V: Part1.+5V, Raspberry_Pi_1.5V
  N16: Part1.TXD, Raspberry_Pi_1.GPIO14
  N17: Part1.RXD, Raspberry_Pi_1.GPIO15
  N18: Part1.GPIO18, Raspberry_Pi_1.GPIO18, LED2.red_cathode
  N19: Part1.GPIO23, Raspberry_Pi_1.GPIO23, LED2.blue_cathode
  N20: Part1.GPIO24, Raspberry_Pi_1.GPIO24, LED2.green_cathode
  N21: Part1.GPIO25, Raspberry_Pi_1.GPIO25
  N22: Part1.CE0, Raspberry_Pi_1.GPIO8
  N23: Part1.CE1, Raspberry_Pi_1.GPIO7
  N24: Part1.EECLK, Raspberry_Pi_1.ID_SC
  N25: Part1.GPIO12, Raspberry_Pi_1.GPIO12
  N26: Part1.GPIO16, Raspberry_Pi_1.GPIO16
  N27: Part1.GPIO20, Raspberry_Pi_1.GPIO20
  N28: Part1.GPIO21, Raspberry_Pi_1.GPIO21
  N29: Part2.D9_PWM, R4.Pin_0
  N30: Part2.D10_PWM/SS, R5.Pin_0
  N31: Part2.D11_PWM/MOSI, R3.Pin_0
  N32: Part2.GND, LED1.common_anode
  N33: LED1.red_cathode, R3.Pin_1
  N34: LED1.blue_cathode, R5.Pin_1
  N35: LED1.green_cathode, R4.Pin_1

notes:
  Connect RaspberryPi to Arduino: USB-A to USB-B
  RaspberryPi: USB-A Arduino: USB-B
  RaspberryPi will power the Arduino and send commands via USB Serial.
  Micro-USB Power
  5V / 2.5A
  ARDUINO
  RASPBERRY PI

custom parts:
  Adafruit T-Cobbler Plus: The Raspberry Pi has landed on the Maker World like a 40-GPIO pinned, quad-USB ported, credit card sized bomb of DIY joy. And while you can use most of our great Model B accessories by hooking up our downgrade cable, its probably a good time to upgrade your set up and accessorize using all of the 40 pins. That's why we now carry the Assembled Adafruit Pi T-Cobbler Plus - Breakout + Cable for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
